// Logisim project PROTTOY2207005.circ as structural Verilog: 33 circuits, main circuit main
module main (
  input  [1:0] in_1,
  input  [18:0] in_2,
  input  [18:0] in_3,
  output [18:0] out_4,
  output ZERO,
  output CARRY,
  output NEGATIVE,
  output OVERFLOW,
  output [3:0] out_9
);

  wire zero_1_out_2;
  wire [18:0] and_1_out_3, n19_bit_adder_1_out_4, or_1_out_3;

  AND and_1 (.in_1(in_2), .in_2(in_3), .out_3(and_1_out_3));
  OR or_1 (.in_1(in_2), .in_2(in_3), .out_3(or_1_out_3));
  _19_BIT_ADDER u_19_bit_adder_1 (
    .in_1(in_1[0]), .in_2(in_2), .in_3(in_3), .out_4(n19_bit_adder_1_out_4), .out_5(CARRY), .out_6(out_9[3]));
  Multiplexer #(.select(2), .width(19), .enable("false")) multiplexer_1 (
    .in0(and_1_out_3), .in1(or_1_out_3), .in2(n19_bit_adder_1_out_4), .in3(n19_bit_adder_1_out_4),
    .out(out_4), .sel(in_1));
  ZERO zero_1 (.in_1(out_4), .out_2(zero_1_out_2));
  NEGATIVE negative_1 (.in_1(out_4), .out_2(NEGATIVE));
  not not_1 (out_9[0], zero_1_out_2);

  assign out_9[2:1] = {CARRY, NEGATIVE};
  assign OVERFLOW = out_9[3];
  assign ZERO = out_9[0];

  // Notes on the sheet:
  //   A
  //   B
  //   00-AND
  //   01-OR
  //   10-ADDER
  //   11-SUBTRACT
  //   2207005
  //   AND
  //   OR
  //   OVERFLOW
  //   -
  //   CARRY
  //   -
  //   NEGATIVE
  //   -
  //   ZERO
endmodule

module AND (
  input  [18:0] in_1,
  input  [18:0] in_2,
  output [18:0] out_3
);

  assign out_3 = in_1 & in_2;  // AND_Gate and_1, 19 bits wide

  // Notes on the sheet:
  //   2207005
endmodule

module OR (
  input  [18:0] in_1,
  input  [18:0] in_2,
  output [18:0] out_3
);

  assign out_3 = in_1 | in_2;  // OR_Gate or_1, 19 bits wide

  // Notes on the sheet:
  //   2207005
endmodule

module ZERO (
  input  [18:0] in_1,
  output out_2
);

  or or_1 (out_2, in_1[0], in_1[1], in_1[2], in_1[3], in_1[4], in_1[5], in_1[6], in_1[7], in_1[8], in_1[9], in_1[10], in_1[11], in_1[12], in_1[13], in_1[14], in_1[15], in_1[16], in_1[17], in_1[18]);
endmodule

module NEGATIVE (
  input  [18:0] in_1,
  output out_2
);


  assign out_2 = in_1[18];

  // Notes on the sheet:
  //   2207005
endmodule

module _4_BIT_CLA (
  input  Cin,
  input  [3:0] A,
  input  [3:0] B,
  output [3:0] out_4,
  output out_5
);

  wire and_1_out, and_2_out, and_3_out, and_4_out, and_5_out, and_6_out, and_7_out, and_8_out, and_9_out,
       and_10_out, G0_out, G1_out, G2_out, G3_out, or_1_out, or_2_out, or_3_out, P0_out, P1_out, P2_out,
       P3_out;

  xor P0 (P0_out, A[0], B[0]);
  xor P1 (P1_out, A[1], B[1]);
  xor P2 (P2_out, A[2], B[2]);
  xor P3 (P3_out, A[3], B[3]);
  and G0 (G0_out, A[0], B[0]);
  and G1 (G1_out, A[1], B[1]);
  and G2 (G2_out, A[2], B[2]);
  and G3 (G3_out, A[3], B[3]);
  and and_1 (and_1_out, P0_out, Cin);
  and and_2 (and_2_out, P1_out, G0_out);
  and and_3 (and_3_out, P1_out, Cin, P0_out);
  or or_1 (or_1_out, and_1_out, G0_out);
  or or_2 (or_2_out, and_2_out, G1_out, and_3_out);
  and and_4 (and_4_out, P2_out, G1_out);
  and and_5 (and_5_out, P2_out, P1_out, G0_out);
  and and_6 (and_6_out, P2_out, P0_out, Cin, P1_out);
  and and_7 (and_7_out, P3_out, G2_out);
  and and_8 (and_8_out, G1_out, P2_out, P3_out);
  and and_9 (and_9_out, G0_out, P1_out, P2_out, P3_out);
  and and_10 (and_10_out, Cin, P0_out, P1_out, P2_out, P3_out);
  xor xor_1 (out_4[0], Cin, P0_out);
  xor xor_2 (out_4[1], or_1_out, P1_out);
  xor xor_3 (out_4[2], or_2_out, P2_out);
  or or_3 (or_3_out, and_4_out, and_5_out, and_6_out, G2_out);
  xor xor_4 (out_4[3], P3_out, or_3_out);
  or or_4 (out_5, and_7_out, and_8_out, and_9_out, and_10_out, G3_out);

  // Notes on the sheet:
  //   2207005
endmodule

module _3BIT_CLA (
  input  in_1,
  input  [2:0] in_2,
  input  [2:0] in_3,
  output [2:0] out_4,
  output out_5,
  output out_6
);

  wire and_1_out, and_2_out, and_3_out, and_4_out, and_5_out, and_6_out, G0_out, G1_out, G2_out, or_1_out,
       or_2_out, P0_out, P1_out, P2_out;

  xor P0 (P0_out, in_2[0], in_3[0]);
  xor P1 (P1_out, in_2[1], in_3[1]);
  xor P2 (P2_out, in_2[2], in_3[2]);
  and G0 (G0_out, in_2[0], in_3[0]);
  and G1 (G1_out, in_2[1], in_3[1]);
  and G2 (G2_out, in_2[2], in_3[2]);
  and and_1 (and_1_out, P0_out, in_1);
  and and_2 (and_2_out, P1_out, G0_out);
  and and_3 (and_3_out, P1_out, P0_out, in_1);
  and and_4 (and_4_out, P2_out, G1_out);
  and and_5 (and_5_out, P2_out, P1_out, G0_out);
  and and_6 (and_6_out, P2_out, P1_out, P0_out, in_1);
  or or_1 (or_1_out, and_1_out, G0_out);
  or or_2 (or_2_out, G1_out, and_2_out, and_3_out);
  xor xor_1 (out_4[0], in_1, P0_out);
  or or_3 (out_5, and_4_out, and_5_out, and_6_out, G2_out);
  xor xor_2 (out_4[1], or_1_out, P1_out);
  xor xor_3 (out_4[2], or_2_out, P2_out);
  xor xor_4 (out_6, or_2_out, out_5);

  // Notes on the sheet:
  //   2207005
endmodule

module ADDER (
  input  Cin,
  input  A,
  input  B,
  output SUM,
  output COUT
);

  wire and_1_out, and_2_out, xor_1_out;

  xor xor_1 (xor_1_out, A, B);
  and and_1 (and_1_out, A, B);
  xor xor_2 (SUM, Cin, xor_1_out);
  and and_2 (and_2_out, Cin, xor_1_out);
  xor xor_3 (COUT, and_2_out, and_1_out);

  // Notes on the sheet:
  //   2207005
endmodule

module _19_BIT_ADDER (
  input  in_1,
  input  [18:0] in_2,
  input  [18:0] in_3,
  output [18:0] out_4,
  output out_5,
  output out_6
);

  wire n4_bit_cla_1_out_5, n4_bit_cla_2_out_5, n4_bit_cla_3_out_5, n4_bit_cla_4_out_5;
  wire [2:0] bit_extender_1_out, xor_5_out;
  wire [3:0] bit_extender_2_out, xor_1_out, xor_2_out, xor_3_out, xor_4_out;

  assign bit_extender_1_out = {{2{in_1}}, in_1};  // Bit_Extender bit_extender_1
  assign bit_extender_2_out = {{3{in_1}}, in_1};  // Bit_Extender bit_extender_2
  assign xor_1_out = in_3[3:0] ^ bit_extender_2_out;  // XOR_Gate xor_1, 4 bits wide
  assign xor_2_out = in_3[7:4] ^ bit_extender_2_out;  // XOR_Gate xor_2, 4 bits wide
  assign xor_3_out = in_3[11:8] ^ bit_extender_2_out;  // XOR_Gate xor_3, 4 bits wide
  assign xor_4_out = in_3[15:12] ^ bit_extender_2_out;  // XOR_Gate xor_4, 4 bits wide
  assign xor_5_out = bit_extender_1_out ^ in_3[18:16];  // XOR_Gate xor_5, 3 bits wide
  _4_BIT_CLA u_4_bit_cla_1 (.Cin(in_1), .A(in_2[3:0]), .B(xor_1_out), .out_4(out_4[3:0]), .out_5(n4_bit_cla_1_out_5));
  _4_BIT_CLA u_4_bit_cla_2 (
    .Cin(n4_bit_cla_1_out_5), .A(in_2[7:4]), .B(xor_2_out), .out_4(out_4[7:4]), .out_5(n4_bit_cla_2_out_5));
  _4_BIT_CLA u_4_bit_cla_3 (
    .Cin(n4_bit_cla_2_out_5), .A(in_2[11:8]), .B(xor_3_out), .out_4(out_4[11:8]), .out_5(n4_bit_cla_3_out_5));
  _4_BIT_CLA u_4_bit_cla_4 (
    .Cin(n4_bit_cla_3_out_5), .A(in_2[15:12]), .B(xor_4_out), .out_4(out_4[15:12]), .out_5(n4_bit_cla_4_out_5));
  _3BIT_CLA u_3bit_cla_1 (
    .in_1(n4_bit_cla_4_out_5), .in_2(in_2[18:16]), .in_3(xor_5_out), .out_4(out_4[18:16]), .out_5(out_5),
    .out_6(out_6));

  // Notes on the sheet:
  //   2207005
endmodule

module COUNTER (
  input  [1:0] Q,
  input  [2:0] T,
  input  C,
  output DA,
  output DB,
  output DC
);

  wire and_1_out, and_2_out, and_3_out, and_4_out, and_5_out, or_4_out, or_5_out, Q0, Q1, Q2, Q3, T0, T1, T2,
       T3, T4, T5, T6, T7;

  or or_1 (DA, T0, and_4_out, T3, T4, and_5_out, T7);
  or or_2 (DB, T1, and_1_out, T5, T6, T6, T7);
  or or_3 (DC, T5, and_2_out, T3, T4, and_3_out, T7);
  Decoder #(.select(2), .enable("false")) decoder_1 (.out0(Q0), .out1(Q1), .out2(Q2), .out3(Q3), .sel(Q));
  Decoder #(.select(3), .enable("false")) decoder_2 (
    .out0(T0), .out1(T1), .out2(T2), .out3(T3), .out4(T4), .out5(T5), .out6(T6), .out7(T7), .sel(T));
  and and_1 (and_1_out, T2, Q2);
  and and_2 (and_2_out, T2, or_4_out);
  and and_3 (and_3_out, T6, C);
  and and_4 (and_4_out, T2, or_5_out);
  and and_5 (and_5_out, T6, C);
  or or_4 (or_4_out, Q0, Q1, Q3);
  or or_5 (or_5_out, Q0, Q2, Q3);

  // Notes on the sheet:
  //   2207005
endmodule

module CONTROLLER (
  input  Clk,
  input  Reset,
  input  Q0,
  input  Q_1,
  input  [4:0] Count,
  output Cl__A__Q_1,
  output LOad__M__Q__Cnt,
  output Load_A,
  output C0,
  output C1,
  output Shr,
  output Dec_Cnt
);

  wire counter_1_da, counter_1_db, counter_1_dc, nor_1_out, T0, T2, T4, T6, T7;
  wire [2:0] T;

  nor nor_1 (nor_1_out, Count[2], Count[3], Count[0], Count[1], Count[4]);
  COUNTER counter_1 (.Q({Q0, Q_1}), .T(T), .C(nor_1_out), .DA(counter_1_da), .DB(counter_1_db), .DC(counter_1_dc));
  Decoder #(.select(3), .enable("false")) decoder_1 (
    .out0(T0), .out1(Cl__A__Q_1), .out2(T2), .out3(C0), .out4(T4), .out5(Dec_Cnt), .out6(T6), .out7(T7),
    .sel(T));
  D_Flip_Flop d_ff_1 (.clk(Clk), .D(counter_1_da), .Q(T[0]), .reset(Reset));  // open: Qn, preset, en
  D_Flip_Flop d_ff_2 (.clk(Clk), .D(counter_1_db), .Q(T[1]), .reset(Reset));  // open: Qn, preset, en
  D_Flip_Flop d_ff_3 (.clk(Clk), .D(counter_1_dc), .Q(T[2]), .reset(Reset));  // open: Qn, preset, en
  or or_1 (Load_A, C0, T4);
  or or_2 (C1, T4, C0);

  assign LOad__M__Q__Cnt = Cl__A__Q_1;
  assign Shr = Dec_Cnt;

  // Other names for the same wires on the sheet: T1 = Cl__A__Q_1; T3 = C0; T5 = Dec_Cnt

  // Notes on the sheet:
  //   2207005
endmodule

module _4X1MUX (
  input  [1:0] in_1,
  input  [18:0] in_2,
  input  [18:0] in_3,
  input  [18:0] in_4,
  input  [18:0] in_5,
  output [18:0] out_6
);

  wire [18:0] and_1_out, and_2_out, and_3_out, and_4_out, bit_extender_1_out, bit_extender_2_out, not_1_out,
       not_2_out, not_3_out, not_4_out;

  assign bit_extender_1_out = {{18{in_1[0]}}, in_1[0]};  // Bit_Extender bit_extender_1
  assign bit_extender_2_out = {{18{in_1[1]}}, in_1[1]};  // Bit_Extender bit_extender_2
  assign not_1_out = ~bit_extender_2_out;  // NOT_Gate not_1, 19 bits wide
  assign not_2_out = ~bit_extender_1_out;  // NOT_Gate not_2, 19 bits wide
  assign not_3_out = ~bit_extender_1_out;  // NOT_Gate not_3, 19 bits wide
  assign not_4_out = ~bit_extender_2_out;  // NOT_Gate not_4, 19 bits wide
  assign and_1_out = not_3_out & not_4_out & in_2;  // AND_Gate and_1, 19 bits wide
  assign and_2_out = in_3 & not_1_out & bit_extender_1_out;  // AND_Gate and_2, 19 bits wide
  assign and_3_out = not_2_out & bit_extender_2_out & in_4;  // AND_Gate and_3, 19 bits wide
  assign and_4_out = bit_extender_2_out & bit_extender_1_out & in_5;  // AND_Gate and_4, 19 bits wide
  assign out_6 = and_1_out | and_2_out | and_3_out | and_4_out;  // OR_Gate or_1, 19 bits wide

  // Notes on the sheet:
  //   2207005
endmodule

module _2_S_COMPLEMENT (
  input  [18:0] in_1,
  output [18:0] out_2
);

  wire [17:0] not_1_out;
  wire [18:0] alu_1_out_4;

  not not_1 (not_1_out[0], in_1[0]);
  not not_2 (not_1_out[1], in_1[1]);
  not not_3 (not_1_out[2], in_1[2]);
  not not_4 (not_1_out[3], in_1[3]);
  not not_5 (not_1_out[4], in_1[4]);
  not not_6 (not_1_out[5], in_1[5]);
  not not_7 (not_1_out[6], in_1[6]);
  not not_8 (not_1_out[7], in_1[7]);
  not not_9 (not_1_out[8], in_1[8]);
  not not_10 (not_1_out[9], in_1[9]);
  not not_11 (not_1_out[10], in_1[10]);
  not not_12 (not_1_out[11], in_1[11]);
  not not_13 (not_1_out[12], in_1[12]);
  not not_14 (not_1_out[13], in_1[13]);
  not not_15 (not_1_out[14], in_1[14]);
  not not_16 (not_1_out[15], in_1[15]);
  not not_17 (not_1_out[16], in_1[16]);
  not not_18 (not_1_out[17], in_1[17]);
  Multiplexer #(.width(19), .enable("false")) multiplexer_1 (
    .in0(in_1), .in1(alu_1_out_4), .out(out_2), .sel(in_1[18]));
  ALU alu_1 (.in_1(2'b10), .in_2({in_1[18], not_1_out}), .in_3(19'h1), .out_4(alu_1_out_4));  // open: NEGATIVE, out_6

  // Notes on the sheet:
  //   2207005
endmodule

module ALU (
  input  [1:0] in_1,
  input  [18:0] in_2,
  input  [18:0] in_3,
  output [18:0] out_4,
  output NEGATIVE,
  output [3:0] out_6
);

  wire zero_1_out_2;
  wire [18:0] and_1_out_3, n19_bit_adder_1_out_4, or_1_out_3;

  AND and_1 (.in_1(in_2), .in_2(in_3), .out_3(and_1_out_3));
  OR or_1 (.in_1(in_2), .in_2(in_3), .out_3(or_1_out_3));
  _19_BIT_ADDER u_19_bit_adder_1 (
    .in_1(in_1[0]), .in_2(in_2), .in_3(in_3), .out_4(n19_bit_adder_1_out_4), .out_5(NEGATIVE),
    .out_6(out_6[3]));
  Multiplexer #(.select(2), .width(19), .enable("false")) multiplexer_1 (
    .in0(and_1_out_3), .in1(or_1_out_3), .in2(n19_bit_adder_1_out_4), .in3(n19_bit_adder_1_out_4),
    .out(out_4), .sel(in_1));
  ZERO zero_1 (.in_1(out_4), .out_2(zero_1_out_2));
  NEGATIVE negative_1 (.in_1(out_4), .out_2(out_6[1]));
  not not_1 (out_6[0], zero_1_out_2);

  assign out_6[2] = NEGATIVE;

  // Notes on the sheet:
  //   A
  //   B
  //   00-AND
  //   01-OR
  //   10-ADDER
  //   11-SUBTRACT
  //   2207005
  //   AND
  //   OR
  //   CARRY
  //   OVERFLOW
  //   ZERO
  //   OVERFLOW
  //   -
  //   CARRY
  //   -
  //   NEGATIVE
  //   -
  //   ZERO
endmodule

module BoothMultiplier (
  input  [18:0] in_1,
  input  [18:0] in_2,
  input  in_3,
  output [18:0] out_4,
  output [18:0] out_5
);

  wire clock_1_out, controller_1_cl__a__q_1, controller_1_dec_cnt, controller_1_load__m__q__cnt,
       controller_1_load_a, controller_1_shr, or_1_out, shift_register_1_out, shift_register_3_out,
       shift_register_4_q0;
  wire [1:0] controller_1_c0;
  wire [4:0] counter_1_q;
  wire [18:0] alu_1_out_4, n2_s_complement_1_out_2, n2_s_complement_2_out_2, shift_register_2_q18;

  Clock clock_1 (.out(clock_1_out));
  CONTROLLER controller_1 (
    .Clk(clock_1_out), .Reset(in_3), .Q0(out_5[0]), .Q_1(shift_register_4_q0), .Count(counter_1_q),
    .Cl__A__Q_1(controller_1_cl__a__q_1), .LOad__M__Q__Cnt(controller_1_load__m__q__cnt),
    .Load_A(controller_1_load_a), .C0(controller_1_c0[0]), .C1(controller_1_c0[1]), .Shr(controller_1_shr),
    .Dec_Cnt(controller_1_dec_cnt));
  or or_1 (or_1_out, controller_1_dec_cnt, controller_1_load__m__q__cnt);
  // Probe on in_2
  Counter #(.width(5), .max('h1d)) counter_1 (
    .load(or_1_out), .D(5'b10011), .count(controller_1_dec_cnt), .Q(counter_1_q), .clk(clock_1_out));  // open: carry, clr
  // Probe on in_1
  Shift_Register #(.length(19)) shift_register_1 (
    .shift(controller_1_shr), .in(out_4[18]), .clk(clock_1_out), .out(shift_register_1_out),
    .load(controller_1_load_a), .clr(controller_1_cl__a__q_1), .d0(alu_1_out_4[18]), .q0(out_4[18]),
    .d1(alu_1_out_4[17]), .q1(out_4[17]), .d2(alu_1_out_4[16]), .q2(out_4[16]), .d3(alu_1_out_4[15]),
    .q3(out_4[15]), .d4(alu_1_out_4[14]), .q4(out_4[14]), .d5(alu_1_out_4[13]), .q5(out_4[13]),
    .d6(alu_1_out_4[12]), .q6(out_4[12]), .d7(alu_1_out_4[11]), .q7(out_4[11]), .d8(alu_1_out_4[10]),
    .q8(out_4[10]), .d9(alu_1_out_4[9]), .q9(out_4[9]), .d10(alu_1_out_4[8]), .q10(out_4[8]),
    .d11(alu_1_out_4[7]), .q11(out_4[7]), .d12(alu_1_out_4[6]), .q12(out_4[6]), .d13(alu_1_out_4[5]),
    .q13(out_4[5]), .d14(alu_1_out_4[4]), .q14(out_4[4]), .d15(alu_1_out_4[3]), .q15(out_4[3]),
    .d16(alu_1_out_4[2]), .q16(out_4[2]), .d17(alu_1_out_4[1]), .q17(out_4[1]), .d18(alu_1_out_4[0]),
    .q18(out_4[0]));
  _2_S_COMPLEMENT u_2_s_complement_1 (.in_1(in_1), .out_2(n2_s_complement_1_out_2));
  _2_S_COMPLEMENT u_2_s_complement_2 (.in_1(in_2), .out_2(n2_s_complement_2_out_2));
  Shift_Register #(.length(19)) shift_register_2 (
    .shift(1'b0), .clk(clock_1_out), .load(controller_1_load__m__q__cnt), .d0(n2_s_complement_1_out_2[18]),
    .q0(shift_register_2_q18[18]), .d1(n2_s_complement_1_out_2[17]), .q1(shift_register_2_q18[17]),
    .d2(n2_s_complement_1_out_2[16]), .q2(shift_register_2_q18[16]), .d3(n2_s_complement_1_out_2[15]),
    .q3(shift_register_2_q18[15]), .d4(n2_s_complement_1_out_2[14]), .q4(shift_register_2_q18[14]),
    .d5(n2_s_complement_1_out_2[13]), .q5(shift_register_2_q18[13]), .d6(n2_s_complement_1_out_2[12]),
    .q6(shift_register_2_q18[12]), .d7(n2_s_complement_1_out_2[11]), .q7(shift_register_2_q18[11]),
    .d8(n2_s_complement_1_out_2[10]), .q8(shift_register_2_q18[10]), .d9(n2_s_complement_1_out_2[9]),
    .q9(shift_register_2_q18[9]), .d10(n2_s_complement_1_out_2[8]), .q10(shift_register_2_q18[8]),
    .d11(n2_s_complement_1_out_2[7]), .q11(shift_register_2_q18[7]), .d12(n2_s_complement_1_out_2[6]),
    .q12(shift_register_2_q18[6]), .d13(n2_s_complement_1_out_2[5]), .q13(shift_register_2_q18[5]),
    .d14(n2_s_complement_1_out_2[4]), .q14(shift_register_2_q18[4]), .d15(n2_s_complement_1_out_2[3]),
    .q15(shift_register_2_q18[3]), .d16(n2_s_complement_1_out_2[2]), .q16(shift_register_2_q18[2]),
    .d17(n2_s_complement_1_out_2[1]), .q17(shift_register_2_q18[1]), .d18(n2_s_complement_1_out_2[0]),
    .q18(shift_register_2_q18[0]));  // open: in, out, clr
  Shift_Register #(.length(19)) shift_register_3 (
    .shift(controller_1_shr), .in(shift_register_1_out), .clk(clock_1_out), .out(shift_register_3_out),
    .load(controller_1_load__m__q__cnt), .d0(n2_s_complement_2_out_2[18]), .q0(out_5[18]),
    .d1(n2_s_complement_2_out_2[17]), .q1(out_5[17]), .d2(n2_s_complement_2_out_2[16]), .q2(out_5[16]),
    .d3(n2_s_complement_2_out_2[15]), .q3(out_5[15]), .d4(n2_s_complement_2_out_2[14]), .q4(out_5[14]),
    .d5(n2_s_complement_2_out_2[13]), .q5(out_5[13]), .d6(n2_s_complement_2_out_2[12]), .q6(out_5[12]),
    .d7(n2_s_complement_2_out_2[11]), .q7(out_5[11]), .d8(n2_s_complement_2_out_2[10]), .q8(out_5[10]),
    .d9(n2_s_complement_2_out_2[9]), .q9(out_5[9]), .d10(n2_s_complement_2_out_2[8]), .q10(out_5[8]),
    .d11(n2_s_complement_2_out_2[7]), .q11(out_5[7]), .d12(n2_s_complement_2_out_2[6]), .q12(out_5[6]),
    .d13(n2_s_complement_2_out_2[5]), .q13(out_5[5]), .d14(n2_s_complement_2_out_2[4]), .q14(out_5[4]),
    .d15(n2_s_complement_2_out_2[3]), .q15(out_5[3]), .d16(n2_s_complement_2_out_2[2]), .q16(out_5[2]),
    .d17(n2_s_complement_2_out_2[1]), .q17(out_5[1]), .d18(n2_s_complement_2_out_2[0]), .q18(out_5[0]));  // open: clr
  // Probe on out_5
  ALU alu_1 (
    .in_1(controller_1_c0), .in_2(out_4), .in_3(shift_register_2_q18), .out_4(alu_1_out_4));  // open: NEGATIVE, out_6
  Shift_Register #(.length(1)) shift_register_4 (
    .shift(controller_1_shr), .in(shift_register_3_out), .clk(clock_1_out), .clr(controller_1_cl__a__q_1),
    .q0(shift_register_4_q0));  // open: out, load, d0

  // Notes on the sheet:
  //   2207005
endmodule

// 2PLR
module _2bit_plr (
  input  in_1,
  input  [1:0] in_2,
  input  CLK,
  input  CLR,
  output [1:0] out_5
);

  wire and_1_out, and_2_out, and_3_out, and_4_out, not_1_out, not_2_out;

  not not_1 (not_1_out, in_2[1]);
  not not_2 (not_2_out, in_2[0]);
  and and_1 (and_1_out, in_2[0], in_1);
  and and_2 (and_2_out, not_2_out, in_1);
  and and_3 (and_3_out, in_2[1], in_1);
  and and_4 (and_4_out, not_1_out, in_1);
  J_K_Flip_Flop j_k_ff_1 (.J(and_1_out), .clk(CLK), .K(and_2_out), .Q(out_5[0]), .reset(CLR));  // open: Qn, preset, en
  J_K_Flip_Flop j_k_ff_2 (.J(and_3_out), .clk(CLK), .K(and_4_out), .Q(out_5[1]), .reset(CLR));  // open: Qn, preset, en

  // Notes on the sheet:
  //   2207005
endmodule

// 3PLR
module _3BIT_PLR (
  input  in_1,
  input  [2:0] in_2,
  input  CLK,
  input  CLR,
  output [2:0] out_5
);

  wire and_1_out, and_2_out, and_3_out, and_4_out, and_5_out, and_6_out, not_1_out, not_2_out, not_3_out;

  not not_1 (not_1_out, in_2[1]);
  not not_2 (not_2_out, in_2[0]);
  not not_3 (not_3_out, in_2[2]);
  and and_1 (and_1_out, in_2[0], in_1);
  and and_2 (and_2_out, not_2_out, in_1);
  and and_3 (and_3_out, in_2[1], in_1);
  and and_4 (and_4_out, not_1_out, in_1);
  and and_5 (and_5_out, in_1, in_2[2]);
  and and_6 (and_6_out, in_1, not_3_out);
  J_K_Flip_Flop j_k_ff_1 (.J(and_1_out), .clk(CLK), .K(and_2_out), .Q(out_5[0]), .reset(CLR));  // open: Qn, preset, en
  J_K_Flip_Flop j_k_ff_2 (.J(and_3_out), .clk(CLK), .K(and_4_out), .Q(out_5[1]), .reset(CLR));  // open: Qn, preset, en
  J_K_Flip_Flop j_k_ff_3 (.J(and_5_out), .clk(CLK), .K(and_6_out), .Q(out_5[2]), .reset(CLR));  // open: Qn, preset, en

  // Notes on the sheet:
  //   2207005
endmodule

// 4CPL
module _4_BIT_CPL (
  input  CIN,
  input  COUNT,
  input  LOAD,
  input  [3:0] in_4,
  input  in_5,
  input  CLEAR,
  output [3:0] out_7,
  output out_8
);

  wire and_1_out, and_2_out, and_3_out, and_4_out, and_5_out, and_6_out, and_7_out, and_8_out, and_9_out,
       and_10_out, and_11_out, and_12_out, and_13_out, not_1_out, not_2_out, not_3_out, not_4_out, not_5_out,
       or_1_out, or_2_out, or_3_out, or_4_out, or_5_out, or_6_out, or_7_out, or_8_out;

  and and_1 (and_1_out, COUNT, not_1_out);
  not not_1 (not_1_out, LOAD);
  and and_2 (and_2_out, LOAD, in_4[0]);
  and and_3 (and_3_out, LOAD, not_2_out);
  not not_2 (not_2_out, in_4[0]);
  and and_4 (and_4_out, LOAD, in_4[1]);
  and and_5 (and_5_out, LOAD, not_3_out);
  not not_3 (not_3_out, in_4[1]);
  and and_6 (and_6_out, LOAD, in_4[2]);
  and and_7 (and_7_out, LOAD, not_4_out);
  not not_4 (not_4_out, in_4[2]);
  and and_8 (and_8_out, LOAD, in_4[3]);
  and and_9 (and_9_out, LOAD, not_5_out);
  not not_5 (not_5_out, in_4[3]);
  and and_10 (and_10_out, and_1_out, CIN);
  and and_11 (and_11_out, and_1_out, CIN, out_7[0]);
  and and_12 (and_12_out, and_1_out, CIN, out_7[0], out_7[1]);
  and and_13 (and_13_out, and_1_out, CIN, out_7[0], out_7[1], out_7[2]);
  or or_1 (or_1_out, and_2_out, and_10_out);
  or or_2 (or_2_out, and_10_out, and_3_out);
  or or_3 (or_3_out, and_4_out, and_11_out);
  or or_4 (or_4_out, and_11_out, and_5_out);
  or or_5 (or_5_out, and_6_out, and_12_out);
  or or_6 (or_6_out, and_12_out, and_7_out);
  or or_7 (or_7_out, and_8_out, and_13_out);
  or or_8 (or_8_out, and_13_out, and_9_out);
  J_K_Flip_Flop j_k_ff_1 (.J(or_7_out), .clk(in_5), .K(or_8_out), .Q(out_7[3]), .reset(CLEAR));  // open: Qn, preset, en
  J_K_Flip_Flop j_k_ff_2 (.J(or_1_out), .clk(in_5), .K(or_2_out), .Q(out_7[0]), .reset(CLEAR));  // open: Qn, preset, en
  J_K_Flip_Flop j_k_ff_3 (.J(or_3_out), .clk(in_5), .K(or_4_out), .Q(out_7[1]), .reset(CLEAR));  // open: Qn, preset, en
  J_K_Flip_Flop j_k_ff_4 (.J(or_5_out), .clk(in_5), .K(or_6_out), .Q(out_7[2]), .reset(CLEAR));  // open: Qn, preset, en
  and and_14 (out_8, out_7[3], out_7[2], out_7[1], out_7[0], CIN, and_1_out);

  // Notes on the sheet:
  //   CLOCK
  //   2207005
endmodule

// 3 CPL
module _3_BIT_CPL (
  input  CIN,
  input  COUNT,
  input  LOAD,
  input  [2:0] in_4,
  input  CLOCK,
  input  CLEAR,
  output [2:0] out_7
);

  wire and_1_out, and_2_out, and_3_out, and_4_out, and_5_out, and_6_out, and_7_out, and_8_out, and_9_out,
       and_10_out, not_1_out, not_2_out, not_3_out, not_4_out, or_1_out, or_2_out, or_3_out, or_4_out,
       or_5_out, or_6_out;

  and and_1 (and_1_out, COUNT, not_1_out);
  not not_1 (not_1_out, LOAD);
  and and_2 (and_2_out, LOAD, in_4[0]);
  and and_3 (and_3_out, LOAD, not_2_out);
  not not_2 (not_2_out, in_4[0]);
  and and_4 (and_4_out, LOAD, in_4[1]);
  and and_5 (and_5_out, LOAD, not_3_out);
  not not_3 (not_3_out, in_4[1]);
  and and_6 (and_6_out, LOAD, in_4[2]);
  and and_7 (and_7_out, LOAD, not_4_out);
  not not_4 (not_4_out, in_4[2]);
  and and_8 (and_8_out, and_1_out, CIN);
  and and_9 (and_9_out, and_1_out, CIN, out_7[0]);
  and and_10 (and_10_out, and_1_out, CIN, out_7[0], out_7[1]);
  or or_1 (or_1_out, and_2_out, and_8_out);
  or or_2 (or_2_out, and_8_out, and_3_out);
  or or_3 (or_3_out, and_4_out, and_9_out);
  or or_4 (or_4_out, and_9_out, and_5_out);
  or or_5 (or_5_out, and_6_out, and_10_out);
  or or_6 (or_6_out, and_10_out, and_7_out);
  J_K_Flip_Flop j_k_ff_1 (
    .J(or_1_out), .clk(CLOCK), .K(or_2_out), .Q(out_7[0]), .reset(CLEAR));  // open: Qn, preset, en
  J_K_Flip_Flop j_k_ff_2 (
    .J(or_3_out), .clk(CLOCK), .K(or_4_out), .Q(out_7[1]), .reset(CLEAR));  // open: Qn, preset, en
  J_K_Flip_Flop j_k_ff_3 (
    .J(or_5_out), .clk(CLOCK), .K(or_6_out), .Q(out_7[2]), .reset(CLEAR));  // open: Qn, preset, en

  // Notes on the sheet:
  //   2207005
endmodule

// 2CPL
module _2BIT_CPL (
  input  Cin,
  input  Count,
  input  Load,
  input  [1:0] in_4,
  input  Clk,
  input  clr,
  output [1:0] out_7
);

  wire and_1_out, and_2_out, and_3_out, and_4_out, and_5_out, and_6_out, and_7_out, and_8_out, not_1_out,
       not_2_out, not_3_out, not_4_out, or_1_out, or_2_out, or_3_out, or_4_out;

  not not_1 (not_1_out, Load);
  not not_2 (not_2_out, Load);
  and and_1 (and_1_out, Count, not_1_out);
  not not_3 (not_3_out, in_4[0]);
  and and_2 (and_2_out, Count, not_2_out);
  not not_4 (not_4_out, in_4[1]);
  and and_3 (and_3_out, Load, in_4[0]);
  and and_4 (and_4_out, Load, not_3_out);
  and and_5 (and_5_out, Load, in_4[1]);
  and and_6 (and_6_out, Load, not_4_out);
  and and_7 (and_7_out, and_1_out, Cin);
  and and_8 (and_8_out, and_2_out, Cin);
  or or_1 (or_1_out, and_3_out, and_7_out);
  or or_2 (or_2_out, and_7_out, and_4_out);
  or or_3 (or_3_out, and_5_out, and_8_out);
  or or_4 (or_4_out, and_8_out, and_6_out);
  J_K_Flip_Flop j_k_ff_1 (.J(or_1_out), .clk(Clk), .K(or_2_out), .Q(out_7[0]), .reset(clr));  // open: Qn, preset, en
  J_K_Flip_Flop j_k_ff_2 (.J(or_3_out), .clk(Clk), .K(or_4_out), .Q(out_7[1]), .reset(clr));  // open: Qn, preset, en

  // Notes on the sheet:
  //   2207005
endmodule

// 1PLR
module _1_BIT_PLR (
  input  LOAD,
  input  in_2,
  input  CLK,
  input  CLR,
  output out_5
);

  wire and_1_out, and_2_out, not_1_out;

  not not_1 (not_1_out, in_2);
  and and_1 (and_1_out, LOAD, in_2);
  and and_2 (and_2_out, LOAD, not_1_out);
  J_K_Flip_Flop j_k_ff_1 (.J(and_1_out), .clk(CLK), .K(and_2_out), .Q(out_5), .reset(CLR));  // open: Qn, preset, en

  // Notes on the sheet:
  //   2207005
endmodule

// 4 PLR
module _4_BIT_PLR (
  input  in_1,
  input  [3:0] in_2,
  input  CLK,
  input  CLR,
  output [3:0] out_5
);

  wire and_1_out, and_2_out, and_3_out, and_4_out, and_5_out, and_6_out, and_7_out, and_8_out, not_1_out,
       not_2_out, not_3_out, not_4_out;

  not not_1 (not_1_out, in_2[1]);
  not not_2 (not_2_out, in_2[0]);
  not not_3 (not_3_out, in_2[2]);
  not not_4 (not_4_out, in_2[3]);
  and and_1 (and_1_out, in_2[0], in_1);
  and and_2 (and_2_out, not_2_out, in_1);
  and and_3 (and_3_out, in_2[1], in_1);
  and and_4 (and_4_out, not_1_out, in_1);
  and and_5 (and_5_out, in_1, in_2[2]);
  and and_6 (and_6_out, in_1, not_3_out);
  and and_7 (and_7_out, in_1, in_2[3]);
  and and_8 (and_8_out, in_1, not_4_out);
  J_K_Flip_Flop j_k_ff_1 (.J(and_1_out), .clk(CLK), .K(and_2_out), .Q(out_5[0]), .reset(CLR));  // open: Qn, preset, en
  J_K_Flip_Flop j_k_ff_2 (.J(and_3_out), .clk(CLK), .K(and_4_out), .Q(out_5[1]), .reset(CLR));  // open: Qn, preset, en
  J_K_Flip_Flop j_k_ff_3 (.J(and_5_out), .clk(CLK), .K(and_6_out), .Q(out_5[2]), .reset(CLR));  // open: Qn, preset, en
  J_K_Flip_Flop j_k_ff_4 (.J(and_7_out), .clk(CLK), .K(and_8_out), .Q(out_5[3]), .reset(CLR));  // open: Qn, preset, en

  // Notes on the sheet:
  //   2207005
endmodule

module IR (
  input  LOAD,
  input  [3:0] in_2,
  input  CLK,
  input  CLR,
  output [3:0] out_5
);

  wire and_1_out, and_2_out, and_3_out, and_4_out, and_5_out, and_6_out, and_7_out, and_8_out, not_1_out,
       not_2_out, not_3_out, not_4_out;

  not not_1 (not_1_out, in_2[0]);
  not not_2 (not_2_out, in_2[1]);
  not not_3 (not_3_out, in_2[2]);
  not not_4 (not_4_out, in_2[3]);
  and and_1 (and_1_out, in_2[0], LOAD);
  and and_2 (and_2_out, not_1_out, LOAD);
  and and_3 (and_3_out, in_2[1], LOAD);
  and and_4 (and_4_out, not_2_out, LOAD);
  and and_5 (and_5_out, in_2[2], LOAD);
  and and_6 (and_6_out, not_3_out, LOAD);
  and and_7 (and_7_out, in_2[3], LOAD);
  and and_8 (and_8_out, not_4_out, LOAD);
  J_K_Flip_Flop j_k_ff_1 (.J(and_1_out), .clk(CLK), .K(and_2_out), .Q(out_5[0]), .reset(CLR));  // open: Qn, preset, en
  J_K_Flip_Flop j_k_ff_2 (.J(and_3_out), .clk(CLK), .K(and_4_out), .Q(out_5[1]), .reset(CLR));  // open: Qn, preset, en
  J_K_Flip_Flop j_k_ff_3 (.J(and_5_out), .clk(CLK), .K(and_6_out), .Q(out_5[2]), .reset(CLR));  // open: Qn, preset, en
  J_K_Flip_Flop j_k_ff_4 (.J(and_7_out), .clk(CLK), .K(and_8_out), .Q(out_5[3]), .reset(CLR));  // open: Qn, preset, en

  // Notes on the sheet:
  //   2207005
endmodule

module MAR (
  input  in_1,
  input  [5:0] in_2,
  input  in_3,
  input  in_4,
  output [5:0] out_5
);

  wire clock_1_out;

  Clock clock_1 (.out(clock_1_out));
  _4_BIT_PLR u_4_bit_plr_1 (.in_1(in_1), .in_2(in_2[3:0]), .CLK(clock_1_out), .CLR(in_4), .out_5(out_5[3:0]));
  _2bit_plr u_2bit_plr_1 (.in_1(in_1), .in_2(in_2[5:4]), .CLK(clock_1_out), .CLR(in_4), .out_5(out_5[5:4]));

  // Notes on the sheet:
  //   2207005
endmodule

module MBR (
  input  LOAD,
  input  COUNT,
  input  [18:0] in_3,
  input  in_4,
  input  CLR,
  output [18:0] out_6
);

  wire CLK_out, n4_bit_cpl_1_out_8, n4_bit_cpl_2_out_8, n4_bit_cpl_3_out_8, n4_bit_cpl_4_out_8;

  Clock CLK (.out(CLK_out));
  _4_BIT_CPL u_4_bit_cpl_1 (
    .CIN(COUNT), .COUNT(COUNT), .LOAD(LOAD), .in_4(in_3[3:0]), .in_5(CLK_out), .CLEAR(CLR),
    .out_7(out_6[3:0]), .out_8(n4_bit_cpl_1_out_8));
  _4_BIT_CPL u_4_bit_cpl_2 (
    .CIN(n4_bit_cpl_1_out_8), .COUNT(COUNT), .LOAD(LOAD), .in_4(in_3[7:4]), .in_5(CLK_out), .CLEAR(CLR),
    .out_7(out_6[7:4]), .out_8(n4_bit_cpl_2_out_8));
  _4_BIT_CPL u_4_bit_cpl_3 (
    .CIN(n4_bit_cpl_2_out_8), .COUNT(COUNT), .LOAD(LOAD), .in_4(in_3[11:8]), .in_5(CLK_out), .CLEAR(CLR),
    .out_7(out_6[11:8]), .out_8(n4_bit_cpl_3_out_8));
  _4_BIT_CPL u_4_bit_cpl_4 (
    .CIN(n4_bit_cpl_3_out_8), .COUNT(COUNT), .LOAD(LOAD), .in_4(in_3[15:12]), .in_5(CLK_out), .CLEAR(CLR),
    .out_7(out_6[15:12]), .out_8(n4_bit_cpl_4_out_8));
  _3_BIT_CPL u_3_bit_cpl_1 (
    .CIN(n4_bit_cpl_4_out_8), .COUNT(COUNT), .LOAD(LOAD), .in_4(in_3[18:16]), .CLOCK(CLK_out), .CLEAR(CLR),
    .out_7(out_6[18:16]));

  // Notes on the sheet:
  //   2207005
endmodule

module AC (
  input  LOAD,
  input  [18:0] in_2,
  input  in_3,
  input  CLR,
  output [18:0] out_5
);

  wire CLK_out;

  Clock CLK (.out(CLK_out));
  _4_BIT_PLR u_4_bit_plr_1 (.in_1(LOAD), .in_2(in_2[3:0]), .CLK(CLK_out), .CLR(CLR), .out_5(out_5[3:0]));
  _4_BIT_PLR u_4_bit_plr_2 (.in_1(LOAD), .in_2(in_2[7:4]), .CLK(CLK_out), .CLR(CLR), .out_5(out_5[7:4]));
  _4_BIT_PLR u_4_bit_plr_3 (.in_1(LOAD), .in_2(in_2[11:8]), .CLK(CLK_out), .CLR(CLR), .out_5(out_5[11:8]));
  _4_BIT_PLR u_4_bit_plr_4 (.in_1(LOAD), .in_2(in_2[15:12]), .CLK(CLK_out), .CLR(CLR), .out_5(out_5[15:12]));
  _2bit_plr u_2bit_plr_1 (.in_1(LOAD), .in_2(in_2[17:16]), .CLK(CLK_out), .CLR(CLR), .out_5(out_5[17:16]));
  _1_BIT_PLR u_1_bit_plr_1 (.LOAD(LOAD), .in_2(in_2[18]), .CLK(CLK_out), .CLR(CLR), .out_5(out_5[18]));

  // Notes on the sheet:
  //   2207005
endmodule

module PC (
  input  LOAD,
  input  COUNT,
  input  [5:0] in_3,
  input  in_4,
  input  CLR,
  output [5:0] out_6
);

  wire CLK_out, n4_bit_cpl_1_out_8;

  Clock CLK (.out(CLK_out));
  _4_BIT_CPL u_4_bit_cpl_1 (
    .CIN(COUNT), .COUNT(COUNT), .LOAD(LOAD), .in_4(in_3[3:0]), .in_5(CLK_out), .CLEAR(CLR),
    .out_7(out_6[3:0]), .out_8(n4_bit_cpl_1_out_8));
  _2BIT_CPL u_2bit_cpl_1 (
    .Cin(n4_bit_cpl_1_out_8), .Count(COUNT), .Load(LOAD), .in_4(in_3[5:4]), .Clk(CLK_out), .clr(CLR),
    .out_7(out_6[5:4]));

  // Notes on the sheet:
  //   2207005
endmodule

module CONTROLUNIT (
  input  clock,
  input  reset,
  input  F,
  input  [3:0] IR,
  input  BZERO,
  output AC1,
  output BM,
  output C1,
  output IB,
  output F1,
  output PCB,
  output MARB,
  output F0,
  output REStoACC,
  output TAtoB,
  output MB,
  output b_plus_plus,
  output CA,
  output BPC,
  output load,
  output hlt,
  output \nand ,
  output \xor 
);

  wire _101, _120, and_3_out, and_5_out, and_7_out, and_12_out, and_15_out, and_16_out, and_18_out,
       not_2_out, not_3_out, not_4_out, not_5_out, or_1_out, or_2_out, or_5_out, q0, q1, q2, q3, q4, q5, q6,
       q7, q8, q9, q10, q11, t0, t1, t2, t3;
  wire [1:0] counter_1_q;

  Decoder #(.select(4)) decoder_1 (
    .out0(q0), .out1(q1), .out2(q2), .out3(q3), .out4(q4), .out5(q5), .out6(q6), .out7(q7), .out8(q8),
    .out9(q9), .out10(q10), .out11(q11), .sel(IR));  // open: out12, out13, out14, out15, en
  Counter #(.width(2), .max('h3)) counter_1 (
    .load(1'b0), .Q(counter_1_q), .clk(clock), .clr(reset));  // open: D, count, carry
  and and_1 (MARB, F, t0);
  and and_2 (F0, F, t3);
  and and_3 (and_3_out, F, q0, t3);
  or or_1 (or_1_out, q1, q8, q9, q11);
  and and_4 (TAtoB, F, q2, t2);
  and and_5 (and_5_out, F, q2, t3);
  and and_6 (b_plus_plus, F, q3, t2);
  and and_7 (and_7_out, F, q3, t3);
  and and_8 (_120, F, q3, t3, BZERO);
  and and_9 (_101, F, q4, t3);
  and and_10 (BPC, F, q4, t2);
  and and_11 (load, F, q7, t2);
  and and_12 (and_12_out, q6, t3);
  and and_13 (\nand , F, q10, t3);
  and and_14 (\xor , F, q11, t3);
  Decoder #(.select(2)) decoder_2 (.out0(t0), .out1(t1), .out2(t2), .out3(t3), .sel(counter_1_q));  // open: en
  or or_2 (or_2_out, q0, q1, q2, q3, q7, q8, q9, q10, q11);
  and and_15 (and_15_out, F, or_1_out, t3);
  or or_3 (MB, and_5_out, and_7_out, _101);
  and and_16 (and_16_out, F, or_2_out, t1);
  or or_4 (REStoACC, and_3_out, and_15_out);
  not not_1 (hlt, and_12_out);
  not not_2 (not_2_out, F);
  not not_3 (not_3_out, F);
  not not_4 (not_4_out, F);
  and and_17 (AC1, not_2_out, t0);
  and and_18 (and_18_out, not_3_out, t1);
  and and_19 (IB, not_4_out, t2);
  and and_20 (PCB, q5, t3);
  not not_5 (not_5_out, F);
  or or_5 (or_5_out, q0, q1, q2, q3, q7, q8, q9, q10, q11);
  or or_6 (BM, and_18_out, and_16_out);
  or or_7 (C1, and_18_out, _120, _101);
  and and_21 (F1, not_5_out, or_5_out, t3);

  assign CA = BPC;

  // Notes on the sheet:
  //   2207005
endmodule

module BZ (
  input  [18:0] in_1,
  output out_2
);

  nor nor_1 (out_2, in_1[0], in_1[1], in_1[2], in_1[3], in_1[4], in_1[5], in_1[6], in_1[7], in_1[8], in_1[9], in_1[10], in_1[11], in_1[12], in_1[13], in_1[14], in_1[15], in_1[16], in_1[17], in_1[18]);

  // Notes on the sheet:
  //   2207005
endmodule

module NAND (
  input  [18:0] A,
  input  [18:0] B,
  output [18:0] ANANDB
);

  assign ANANDB = ~(A & B);  // NAND_Gate nand_1, 19 bits wide

  // Notes on the sheet:
  //   2207005
endmodule

module XOR (
  input  [18:0] A,
  input  [18:0] B,
  output [18:0] AXORB
);

  assign AXORB = A ^ B;  // XOR_Gate xor_1, 19 bits wide

  // Notes on the sheet:
  //   2207005
endmodule

module ALUSELECTION (
  input  [3:0] IR,
  output c0,
  output c1
);

  Multiplexer #(.select(4), .width(2)) multiplexer_1 (
    .in0(2'b00), .in1(2'b10), .in2(2'b00), .in3(2'b00), .in4(2'b00), .in5(2'b00), .in6(2'b00), .in7(2'b00),
    .in8(2'b01), .in9(2'b11), .in10(2'b00), .in11(2'b00), .in12(2'b00), .in13(2'b00), .in14(2'b00),
    .in15(2'b00), .out({c1, c0}), .sel(IR));  // open: en

  // Notes on the sheet:
  //   2207005
endmodule

module CPU (
  input  reset
);

  wire AC1, alu_1_negative, b_plus_plus, BM, BPC, BZERO, C1, CA, clock, clock_1_out, F0, F1, F_q, hlt, IB,
       load, load_c, MARB, MB, \nand , or_1_out, or_3_out, or_4_out, PCB, REStoACC, S, TAtoB, \xor ;
  wire [1:0] aluselection_1_c0, priority_encoder_1_out, priority_encoder_2_out;
  wire [3:0] IR;
  wire [5:0] MAR, multiplexer_1_out, multiplexer_2_out, PC;
  wire [6:0] undriven;
  wire [18:0] AC, M_output, mbr, multiplexer_3_out, multiplexer_4_out, nandres, res, xorres;

  Clock clock_1 (.out(clock_1_out));
  and and_1 (clock, clock_1_out, S);
  D_Flip_Flop d_ff_1 (.clk(clock), .D(hlt), .Q(S), .reset(reset));  // open: Qn, preset, en
  Multiplexer #(.width(6)) multiplexer_1 (.in0(mbr[5:0]), .in1(PC), .out(multiplexer_1_out), .sel(AC1));  // open: en
  IR ir_1 (.LOAD(IB), .in_2(mbr[18:15]), .CLK(clock), .CLR(reset), .out_5(IR));
  or or_1 (or_1_out, AC1, MARB);
  MAR mar_1 (.in_1(or_1_out), .in_2(multiplexer_1_out), .in_3(clock), .in_4(reset), .out_5(MAR));
  NAND nand_1 (.A(AC), .B(mbr), .ANANDB(nandres));
  XOR xor_1 (.A(AC), .B(mbr), .AXORB(xorres));
  J_K_Flip_Flop F (.J(F1), .clk(clock), .K(F0), .Q(F_q), .reset(reset));  // open: Qn, preset, en
  or or_2 (load_c, PCB, CA);
  Multiplexer #(.width(6)) multiplexer_2 (.in0(MAR), .in1(mbr[5:0]), .out(multiplexer_2_out), .sel(PCB));  // open: en
  CONTROLUNIT controlunit_1 (
    .clock(clock), .reset(reset), .F(F_q), .IR(IR), .BZERO(BZERO), .AC1(AC1), .BM(BM), .C1(C1), .IB(IB),
    .F1(F1), .PCB(PCB), .MARB(MARB), .F0(F0), .REStoACC(REStoACC), .TAtoB(TAtoB), .MB(MB),
    .b_plus_plus(b_plus_plus), .CA(CA), .BPC(BPC), .load(load), .hlt(hlt), .\nand (\nand ), .\xor (\xor ));
  PC pc_1 (.LOAD(load_c), .COUNT(C1), .in_3(multiplexer_2_out), .in_4(clock), .CLR(reset), .out_6(PC));
  or or_3 (or_3_out, load, REStoACC, \nand , \xor );
  Multiplexer #(.select(2), .width(19), .enable("false")) multiplexer_3 (
    .in0(mbr), .in1(res), .in2(nandres), .in3(xorres), .out(multiplexer_3_out), .sel(priority_encoder_1_out));
  Priority_Encoder #(.select(2)) priority_encoder_1 (
    .in0(load), .in1(REStoACC), .in2(\nand ), .in3(\xor ), .out(priority_encoder_1_out));
  Priority_Encoder #(.select(2)) priority_encoder_2 (
    .in0(BM), .in1(TAtoB), .in2(BPC), .out(priority_encoder_2_out));  // open: in3
  or or_4 (or_4_out, BM, TAtoB, BPC);
  Multiplexer #(.select(2), .width(19), .enable("false")) multiplexer_4 (
    .in0(M_output), .in1(AC), .in2({6'b000101, undriven, PC}), .out(multiplexer_4_out),
    .sel(priority_encoder_2_out));  // open: in3
  AC ac_1 (.LOAD(or_3_out), .in_2(multiplexer_3_out), .in_3(clock), .CLR(reset), .out_5(AC));
  MBR mbr_1 (.LOAD(or_4_out), .COUNT(b_plus_plus), .in_3(multiplexer_4_out), .in_4(clock), .CLR(reset), .out_6(mbr));
  // Probe on AC
  ALUSELECTION aluselection_1 (.IR(IR), .c0(aluselection_1_c0[0]), .c1(aluselection_1_c0[1]));
  RAM #(.addrWidth(6), .dataWidth(19), .bus("separate")) ram_1 (
    .addr(MAR), .din(mbr), .data(M_output), .str(MB), .clk(clock), .ld(BM));  // open: sel, clr
  BZ bz_1 (.in_1(mbr), .out_2(BZERO));
  ALU alu_1 (.in_1(aluselection_1_c0), .in_2(AC), .in_3(mbr), .out_4(res), .NEGATIVE(alu_1_negative));  // open: out_6
  D_Flip_Flop d_ff_2 (.clk(clock), .D(alu_1_negative), .reset(reset));  // open: Q, Qn, preset, en

  // Other names for the same wires on the sheet: MBR_address[5:0] = mbr[5:0]; MBR_opcode[3:0] = mbr[18:15]

  // Notes on the sheet:
  //   2207005
endmodule
